# Fritzing sketch MINI ALARAM 423 (saved by Fritzing 0.9.6b)
circuit board: 8.46667cm x 5.64444cm

parts:
  R1 = Resistor [tolerance=±5% power=0.25 resistance=330k package=THT]
  Q1 = NPN-Transistor [package="TO92 [THT]"]
  S3 = SWITCH-MOMENTARY-2 [package=tactile_switch_smd-2]
  Q2 = PNP-Transistor [package="TO92 [THT]"]
  R2 = Resistor [tolerance=±5% power=0.25 resistance=220 package=THT]
  J1 = Piezo Speaker
  C1 = Electrolytic Capacitor [capacitance=47µF voltage=20V package="100 mil [THT, electrolytic]"]
  C2 = Electrolytic Capacitor [capacitance=10nF voltage=6.3V package="100 mil [THT, electrolytic]"]
  BAT1 = Battery Holders [package=battery-aa]

nets:
  N1: R1.Pin_0, Q1.C, Q2.E, Q2.B, C1.+, BAT1.+
  N2: R1.Pin_1, Q1.B, S3.1
  N3: Q1.E, R2.Pin_0, C2.-
  N4: S3.2, Q2.C, R2.Pin_1, J1.pin1, J1.pin2, C1.-, C2.+, BAT1.-
